// Logisim project 4bitAdderSubtractor.circ as structural Verilog
module FA (
  input  A,
  input  B,
  input  Cin,
  output S,
  output Cout
);

  wire and_1_out, and_2_out, xor_1_out;

  xor xor_1 (xor_1_out, A, B);
  and and_1 (and_1_out, A, B);
  and and_2 (and_2_out, xor_1_out, Cin);
  or or_1 (Cout, and_2_out, and_1_out);
  xor xor_2 (S, xor_1_out, Cin);
endmodule

module FourBitAdder (
  input  A3,
  input  A2,
  input  A1,
  input  A0,
  input  B3,
  input  B2,
  input  B1,
  input  B0,
  input  Cin,
  output S3,
  output S2,
  output S1,
  output S0,
  output Carry
);

  wire fa_2_cout, fa_3_cout, fa_4_cout;

  FA fa_1 (.A(A3), .B(B3), .Cin(fa_2_cout), .S(S3), .Cout(Carry));
  FA fa_2 (.A(A2), .B(B2), .Cin(fa_3_cout), .S(S2), .Cout(fa_2_cout));
  FA fa_3 (.A(A1), .B(B1), .Cin(fa_4_cout), .S(S1), .Cout(fa_3_cout));
  FA fa_4 (.A(A0), .B(B0), .Cin(Cin), .S(S0), .Cout(fa_4_cout));

  // Notes on the sheet:
  //   4 bit binary adder
endmodule

module FourBitAdderSubtractor (
  input  A3,
  input  A2,
  input  A1,
  input  A0,
  input  B3,
  input  B2,
  input  B1,
  input  B0,
  input  Mode,
  output S3,
  output S2,
  output S1,
  output S0,
  output Carry
);

  wire fa_2_cout, fa_3_cout, fa_4_cout, xor_1_out, xor_2_out, xor_3_out, xor_4_out;

  xor xor_1 (xor_1_out, B3, Mode);
  FA fa_1 (.A(A3), .B(xor_1_out), .Cin(fa_2_cout), .S(S3), .Cout(Carry));
  xor xor_2 (xor_2_out, B2, Mode);
  FA fa_2 (.A(A2), .B(xor_2_out), .Cin(fa_3_cout), .S(S2), .Cout(fa_2_cout));
  xor xor_3 (xor_3_out, B1, Mode);
  FA fa_3 (.A(A1), .B(xor_3_out), .Cin(fa_4_cout), .S(S1), .Cout(fa_3_cout));
  xor xor_4 (xor_4_out, B0, Mode);
  FA fa_4 (.A(A0), .B(xor_4_out), .Cin(Mode), .S(S0), .Cout(fa_4_cout));

  // Notes on the sheet:
  //   4 bit binary adder/subtractor
endmodule

module fourbitAdderWithOverflow (
  input  A3,
  input  A2,
  input  A1,
  input  A0,
  input  B3,
  input  B2,
  input  B1,
  input  B0,
  input  Cin,
  output S3,
  output S2,
  output S1,
  output S0,
  output Overflow,
  output Carry
);

  wire fa_2_cout, fa_3_cout, fa_4_cout;

  xor xor_1 (Overflow, Carry, fa_2_cout);
  FA fa_1 (.A(A3), .B(B3), .Cin(fa_2_cout), .S(S3), .Cout(Carry));
  FA fa_2 (.A(A2), .B(B2), .Cin(fa_3_cout), .S(S2), .Cout(fa_2_cout));
  FA fa_3 (.A(A1), .B(B1), .Cin(fa_4_cout), .S(S1), .Cout(fa_3_cout));
  FA fa_4 (.A(A0), .B(B0), .Cin(Cin), .S(S0), .Cout(fa_4_cout));

  // Notes on the sheet:
  //   4 bit signed numberbinary adder with overflow detector
endmodule
