// Logisim project parityGeneratorChecker.circ as structural Verilog: 1 circuit, main circuit main
module main (
  input  x,
  input  y,
  input  z,
  input  x0,
  input  y0,
  input  z0,
  output Parity,
  output Error
);

  wire xor_1_out, xor_2_out, xor_3_out;

  xor xor_1 (xor_1_out, z, y);
  xor xor_2 (xor_2_out, z0, y0);
  xor xor_3 (xor_3_out, x0, Parity);
  xnor xnor_1 (Parity, xor_1_out, x);
  xnor xnor_2 (Error, xor_2_out, xor_3_out);

  // Notes on the sheet:
  //   Parity Generator
  //   Parity Checker
endmodule
