// Logisim project registerMemory.circ as structural Verilog: 2 circuits, main circuit main
module main (
  input  [3:0] dataIn,
  input  load,
  input  [3:0] DIn,
  input  LD,
  output [3:0] dataOut,
  output [3:0] DOut
);

  wire and_1_out, clk_out, clock_1_out;

  Clock clock_1 (.out(clock_1_out));
  and and_1 (and_1_out, LD, clock_1_out);
  Clock clk (.out(clk_out));
  Register #(.width(4)) register_1 (.D(dataIn), .en(load), .clk(clk_out), .Q(dataOut));  // open: clr
  D_Flip_Flop d_ff_1 (.D(DIn[0]), .clk(and_1_out), .Q(DOut[0]));  // open: Qn, preset, reset
  D_Flip_Flop d_ff_2 (.D(DIn[1]), .clk(and_1_out), .Q(DOut[1]));  // open: Qn, preset, reset
  D_Flip_Flop d_ff_3 (.D(DIn[2]), .clk(and_1_out), .Q(DOut[2]));  // open: Qn, preset, reset
  D_Flip_Flop d_ff_4 (.D(DIn[3]), .clk(and_1_out), .Q(DOut[3]));  // open: Qn, preset, reset

  // Notes on the sheet:
  //   Register Operation
endmodule

module memory (
);

  RAM #(.addrWidth(4), .dataWidth(4), .databus("bidir")) ram_1 ();  // open: addr, we, oe, clk, data
endmodule
